# Fritzing sketch Contador 1 Digito (saved by Fritzing 0.9.3b)
breadboards: 1

parts:
  S1 = Pushbutton [package="[THT]"]
  S2 = Pushbutton [package="[THT]"]
  S3 = Pushbutton [package="[THT]"]
  Componente1 = Arduino Uno (Rev3)
  R1 = Resistor [tolerance=±5% resistance=1k package=THT]
  R2 = Resistor [tolerance=±5% resistance=1k package=THT]
  R3 = Resistor [tolerance=±5% resistance=1k package=THT]
  R4 = Resistor [tolerance=±5% resistance=220 package=THT]
  7_Segment1 = 7 Segment Display

nets:
  N1: S1.Pin_1, S1.Pin_2
  N2: S1.Pin_3, S1.Pin_4
  N3: S2.Pin_1, S2.Pin_2
  N4: S2.Pin_3, S2.Pin_4
  N5: S3.Pin_1, S3.Pin_2
  N6: S3.Pin_3, S3.Pin_4
  N7: Componente1.D8, 7_Segment1.Segment_G
  N8: Componente1.D9_PWM, 7_Segment1.Segment_F
  N9: Componente1.D10_PWM/SS, 7_Segment1.Segment_A
  N10: Componente1.D11_PWM/MOSI, 7_Segment1.Segment_B
  N11: Componente1.D12/MISO, 7_Segment1.Segment_C
  N12: Componente1.D13/SCK, 7_Segment1.Segment_DP
  N13: Componente1.D3_PWM, R1.Pin_0
  N14: Componente1.D4, R2.Pin_0
  N15: Componente1.D5_PWM, R3.Pin_0
  N16: Componente1.D6_PWM, 7_Segment1.Segment_E
  N17: Componente1.D7, 7_Segment1.Segment_D
  N18: Componente1.GND, R1.Pin_1, R2.Pin_1, R3.Pin_1, R4.Pin_1
  N19: R4.Pin_0, 7_Segment1.common_cathode
