# Fritzing sketch Graduar nivel de luz de 3 LEDs con LDR (saved by Fritzing 0.9.3b)
breadboards: 1

parts:
  Componente1 = Arduino Uno (Rev3)
  S1 = Pushbutton [package="[THT]"]
  R1 = Photocell (LDR) [package=THT]
  R2 = Resistor [tolerance=±5% resistance=1k package=THT]
  R3 = Resistor [tolerance=±5% resistance=220 package=THT]
  LED1 = LED - 5mm [color="Red (633nm)" package="5 mm [THT]"]
  LED2 = LED - 5mm [color="Red (633nm)" package="5 mm [THT]"]
  LED3 = LED - 5mm [color="Red (633nm)" package="5 mm [THT]"]
  R4 = Resistor [tolerance=±5% resistance=220 package=THT]
  R5 = Resistor [tolerance=±5% resistance=220 package=THT]
  R6 = Resistor [tolerance=±5% resistance=220 package=THT]

nets:
  N1: Componente1.A0, R1.pin_1, R3.Pin_0
  N2: Componente1.D8, S1.Pin_1, S1.Pin_2, R2.Pin_0
  N3: Componente1.D9_PWM, LED2.anode
  N4: Componente1.D10_PWM/SS, LED1.anode
  N5: Componente1.D11_PWM/MOSI, LED3.anode
  N6: Componente1.5V, S1.Pin_3, S1.Pin_4, R1.pin_0
  N7: Componente1.GND, R2.Pin_1, R3.Pin_1, R4.Pin_1, R5.Pin_1, R6.Pin_1
  N8: LED1.cathode, R5.Pin_0
  N9: LED2.cathode, R4.Pin_0
  N10: LED3.cathode, R6.Pin_0
